# Fritzing sketch CyLights (saved by Fritzing 0.9.3b)
circuit board: 17.0949cm x 10.0752cm
breadboards: 3

parts:
  Huzzah_ESP8266 = Adafruit HUZZAH ESP8266 [part_number="Adafruit #2471"]
  U1 = AQW214 [package="DIP (Dual Inline) [THT]"]
  U2 = AQW214 [package="DIP (Dual Inline) [THT]"]
  U3 = AQW214 [package="DIP (Dual Inline) [THT]"]
  U4 = AQW214 [package="DIP (Dual Inline) [THT]"]
  U5 = AQW214 [package="DIP (Dual Inline) [THT]"]
  R1 = Resistor [tolerance=±5% resistance=4.7k package=THT]
  C1 = Ceramic Capacitor [capacitance=0.1mF package="100 mil [THT, multilayer]"]
  C2 = Ceramic Capacitor [capacitance=0.1mF package="100 mil [THT, multilayer]"]
  LED1 = LED - 5mm [color="Red (635nm)" package="5 mm [THT]"]
  R2 = Resistor [tolerance=±5% resistance=150 package=THT]
  J1 = Screw terminal - 2 pins [package=THT]
  C3 = Electrolytic Capacitor [capacitance=0.22mF package="100 mil [THT, electrolytic]"]
  C4 = Ceramic Capacitor [capacitance=0.47mF package="100 mil [THT, multilayer]"]
  C5 = Tantalum Capacitor [capacitance=1μF package="100 mil [THT, tantalum]"]
  LED7 = LED - 5mm [color="Yellow (595nm)" package="5 mm [THT]"]
  IC1 = Voltage Regulator [package=to-220-alt]
  IC2 = Voltage Regulator [package=78xxl]
  IC3 = MCP23017 I2C I/O Expander
  J2 = male pin header, 12 pins [form="♂ (male)"]
  J3 = male pin header, 6 pins [form="♂ (male)"]
  LED2 = LED - 3mm [color="Green (570nm)" package="3 mm [THT]"]
  LED3 = LED - 3mm [color="Green (570nm)" package="3 mm [THT]"]
  LED4 = LED - 3mm [color="Green (570nm)" package="3 mm [THT]"]
  LED5 = LED - 3mm [color="Green (570nm)" package="3 mm [THT]"]
  LED6 = LED - 3mm [color="Green (570nm)" package="3 mm [THT]"]
  C6 = Ceramic Capacitor [capacitance=0.1mF package="100 mil [THT, multilayer]"]

nets:
  N1: Huzzah_ESP8266.TX, J3.pin2
  N2: Huzzah_ESP8266.RX, J3.pin3
  N3: Huzzah_ESP8266.VIN, C2.1, LED1.anode, IC2.OUT, J3.pin4, C6.1
  GND: Huzzah_ESP8266.GND, C2.0, R2.Pin_0, J1.pin2, C3.-, C4.0, C5.-, LED7.cathode, IC1.GND, IC2.GND, J2.pin1, J3.pin6, LED2.cathode, LED3.cathode, LED4.cathode, LED5.cathode, LED6.cathode, C6.0
  N4: Huzzah_ESP8266.GPIO16, R1.Pin_0
  N5: Huzzah_ESP8266.GPIO14, LED7.anode
  3.3V: Huzzah_ESP8266.3.3V, C1.1, IC3.VDD
  N6: Huzzah_ESP8266.GPIO4, IC3.SDA
  N7: Huzzah_ESP8266.GPIO5, IC3.SCL
  N8: U1.R1_-_VCC, IC3.GPB1
  N9: U1.R1_-_GND, U1.R2_-_GND, U2.R1_-_GND, U2.R2_-_GND, U3.R1_-_GND, U3.R2_-_GND, U4.R1_-_GND, U4.R2_-_GND, U5.R1_-_GND, U5.R2_-_GND, C1.0, IC3.VSS, IC3.A0, IC3.A1, IC3.A2
  N10: U1.R2_-_VCC, IC3.GPB0
  N11: U1.R2_-_COM, U1.R1_-_COM, U2.R2_-_COM, U2.R1_-_COM, U3.R2_-_COM, U3.R1_-_COM, U4.R2_-_COM, U4.R1_-_COM, U5.R2_-_COM, U5.R1_-_COM, J1.pin1, C4.1, IC1.IN, J2.pin2
  N12: U1.R2_-_NO, J2.pin4
  N13: U1.R1_-_NO, J2.pin3
  N14: U2.R1_-_VCC, IC3.GPB2
  N15: U2.R2_-_VCC, IC3.GPB3
  N16: U2.R2_-_NO, J2.pin6
  N17: U2.R1_-_NO, J2.pin5
  N18: U3.R1_-_VCC, IC3.GPB4
  N19: U3.R2_-_VCC, IC3.GPB5
  N20: U3.R2_-_NO, J2.pin8
  N21: U3.R1_-_NO, J2.pin7
  N22: U4.R1_-_VCC, IC3.GPB6
  N23: U4.R2_-_VCC, IC3.GPB7
  N24: U4.R2_-_NO, J2.pin10
  N25: U4.R1_-_NO, J2.pin9
  N26: U5.R1_-_VCC, IC3.GPA1
  N27: U5.R2_-_VCC, IC3.GPA2
  N28: U5.R2_-_NO, J2.pin12
  N29: U5.R1_-_NO, J2.pin11
  N30: R1.Pin_1, IC3.RESET
  N31: LED1.cathode, R2.Pin_1
  N32: C3.+, C5.+, IC1.OUT, IC2.IN
  N33: IC3.GPA3, LED2.anode
  N34: IC3.GPA4, LED3.anode
  N35: IC3.GPA5, LED4.anode
  N36: IC3.GPA6, LED5.anode
  N37: IC3.GPA7, LED6.anode

notes:
  12VDC IN
  12VDC OUT
  WiFi Act
  PWR
  CyLights, CyLights IoT Control Board, 1.5
  12VDC Out
  12VDC In
  CyLights Board Rev 1.5
  -
  +
  (c) 2019 Cyrus Brunner
  www.cyrusbuilt.net
  FAB 001004 ASSY 001005
  WiFi IoT Remote Outlet Controller
  AQW214
  MCP23017
  Chan 1
  Chan 2
  Chan 3
  Chan 4
  Chan 5
  L1 ON
  L1 OFF
  L2 ON
  L2 OFF
  L3 ON
  L3 OFF
  L4 ON
  TX
  RX
  Vin
  Gnd
  L4 OFF
  L5 ON
  L5 OFF
  LM2940CT
  LM7805
  RS-232

custom parts:
  Adafruit HUZZAH ESP8266: Add Internet to your next project with an adorable, bite-sized WiFi microcontroller, at a price you like! The ESP8266 processor from Espressif is an 80 MHz microcontroller with a full WiFi front-end (both as client and access point) and TCP/IP stack with DNS support as well. While this chip has been very popular, its also been very difficult to use. Most of the low cost modules are not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
  AQW214: Panasonic PhotoMOS Compact DIP8-pin type of 60V to 600V load voltage
  Voltage Regulator: Voltage Regulator Standard LM2940CT 9V regulator. IGO (Input Ground Output).
  MCP23017 I2C I/O Expander: The MCP23017 uses two i2c pins (these can be shared with other i2c devices), and in exchange gives you 16 general purpose pins. You can set each of 16 pins to be input, output, input with a pullup or open drain. There's even the ability to get an interrupt via an external pin when any of the inputs change so you don't have to keep polling the chip.
